# Fritzing sketch Wiring (saved by Fritzing 0.9.10b)
breadboards: 1

parts:
  元件1 = Arduino Uno (Rev3)
  RHT1 = Humidity and Temperature Sensor RHT03
  HC-SR04_Sensor_1 = HC-SR04 Ultrasonic Distance Sensor
  J1 = Basic Servo
  Grove1 = Grove OLED 128x96

nets:
  N1: 元件1.D8, J1.pulse
  N2: 元件1.D11_PWM/MOSI, HC-SR04_Sensor_1.TRIG
  N3: 元件1.D12/MISO, HC-SR04_Sensor_1.ECHO
  GND: 元件1.GND, RHT1.GND_2, HC-SR04_Sensor_1.GND, J1.gnd, Grove1.GND
  N4: 元件1.A4/SDA, Grove1.SDA
  N5: 元件1.A5/SCL, Grove1.SCL
  N6: 元件1.D2, RHT1.Data-signal
  VCC: 元件1.5V, RHT1.Vcc, HC-SR04_Sensor_1.VCC, J1.vcc, Grove1.VCC
